// Logisim project 18 Bit Datapath Design.circ as structural Verilog: 5 circuits, main circuit 18 bit Register File Design
module main (
  input  Binvert,
  input  CarryIn,
  input  in_3,
  input  R_I,
  input  R_I_2,
  input  R_I_3,
  input  in_7,
  input  Mem_ALU_R,
  input  in_9,
  input  in_10,
  input  in_11,
  input  in_12,
  output [17:0] out_13,
  output [17:0] out_14,
  output [4:0] RD,
  output [17:0] out_16,
  output [4:0] RT,
  output [4:0] RS,
  output overflow,
  output [2:0] Opcode,
  output carryOut,
  output [1:0] out_22
);

  wire clock_1_out;
  wire [4:0] multiplexer_1_out;
  wire [17:0] adder_1_out, bit_extender_1_out, multiplexer_2_out, multiplexer_3_out, ram_1_data, register_1_q;

  Register #(.width(18)) register_1 (.D(adder_1_out), .Q(register_1_q), .clk(clock_1_out), .clr(in_3));  // open: en
  Clock clock_1 (.out(clock_1_out));
  Adder #(.width(18)) adder_1 (.a(register_1_q), .b(18'h1), .out(adder_1_out));  // open: cin, cout
  ROM #(.addrWidth(18), .dataWidth(18)) rom_1 (.addr(register_1_q), .data({Opcode, RS, RT, RD}));  // open: sel
  Multiplexer #(.width(5), .enable("false")) multiplexer_1 (.in0(RT), .in1(RD), .out(multiplexer_1_out), .sel(R_I_2));
  assign bit_extender_1_out = {{13{1'b0}}, RD};  // Bit_Extender bit_extender_1
  _18_bit_Register_File_Design u_18_bit_register_file_design_1 (
    .Write_Register(multiplexer_1_out), .read_register_1(RS), .read_data_1(out_14), .read_data_2(out_16),
    .Write_Data(multiplexer_3_out), .read_register_2(RT), .regWrite(R_I_3), .Clock(clock_1_out));
  Bit_Extender #(.in_width(3), .out_width(2)) bit_extender_2 (.in(Opcode), .out(out_22));
  Multiplexer #(.width(18), .enable("false")) multiplexer_2 (
    .in0(out_16), .in1(bit_extender_1_out), .out(multiplexer_2_out), .sel(R_I));
  _18_bit_ALU u_18_bit_alu_1 (
    .B(multiplexer_2_out), .A(out_14), .Binvert(Binvert), .Opcode(out_22), .result(out_13),
    .overflow(overflow), .carryOut(carryOut), .carryIn(CarryIn));  // open: zero
  RAM #(.addrWidth(18), .dataWidth(18), .bus("separate")) ram_1 (
    .addr(out_13), .din(out_16), .data(ram_1_data), .str(in_11), .sel(in_10), .clk(clock_1_out), .ld(in_12),
    .clr(in_9));
  Multiplexer #(.width(18), .enable("false")) multiplexer_3 (
    .in0(ram_1_data), .in1(out_13), .out(multiplexer_3_out), .sel(Mem_ALU_R));

  // Notes on the sheet:
  //   Instruction Memory
  //   contents of rom_1 (hex, n*v repeats v):
  //   881 8881 10881
  //   Accessed Primary Memory
endmodule

module _18_bit_Register_File_Design (
  input  [4:0] Write_Register,
  input  [4:0] read_register_1,
  input  [17:0] Write_Data,
  input  [4:0] read_register_2,
  input  regWrite,
  input  Clock,
  output [17:0] read_data_1,
  output [17:0] read_data_2
);

  wire and_1_out, and_2_out, and_3_out, and_4_out, and_5_out, and_6_out, and_7_out, and_8_out, and_9_out,
       and_10_out, and_11_out, and_12_out, and_13_out, and_14_out, and_15_out, and_16_out, and_17_out,
       and_18_out, decoder_1_out0, decoder_1_out1, decoder_1_out2, decoder_1_out3, decoder_1_out4,
       decoder_1_out5, decoder_1_out6, decoder_1_out7, decoder_1_out8, decoder_1_out9, decoder_1_out10,
       decoder_1_out11, decoder_1_out12, decoder_1_out13, decoder_1_out14, decoder_1_out15, decoder_1_out16,
       decoder_1_out17;
  wire [17:0] register_1_q, register_2_q, register_3_q, register_4_q, register_5_q, register_6_q,
       register_7_q, register_8_q, register_9_q, register_10_q, register_11_q, register_12_q, register_13_q,
       register_14_q, register_15_q, register_16_q, register_17_q, register_18_q;

  Decoder #(.select(5)) decoder_1 (
    .out0(decoder_1_out0), .out1(decoder_1_out1), .out2(decoder_1_out2), .out3(decoder_1_out3),
    .out4(decoder_1_out4), .out5(decoder_1_out5), .out6(decoder_1_out6), .out7(decoder_1_out7),
    .out8(decoder_1_out8), .out9(decoder_1_out9), .out10(decoder_1_out10), .out11(decoder_1_out11),
    .out12(decoder_1_out12), .out13(decoder_1_out13), .out14(decoder_1_out14), .out15(decoder_1_out15),
    .out16(decoder_1_out16), .out17(decoder_1_out17), .sel(Write_Register));  // open: out18, out19, out20, out21, out22, out23, out24, out25, out26, out27, out28, out29, out30, out31, en
  and and_1 (and_1_out, decoder_1_out0, regWrite);
  and and_2 (and_2_out, decoder_1_out1, regWrite);
  and and_3 (and_3_out, decoder_1_out2, regWrite);
  and and_4 (and_4_out, decoder_1_out3, regWrite);
  and and_5 (and_5_out, decoder_1_out4, regWrite);
  and and_6 (and_6_out, decoder_1_out5, regWrite);
  and and_7 (and_7_out, decoder_1_out6, regWrite);
  and and_8 (and_8_out, decoder_1_out7, regWrite);
  and and_9 (and_9_out, decoder_1_out16, regWrite);
  Register #(.width(18)) register_1 (.D(Write_Data), .Q(register_1_q), .clk(Clock), .clr(and_1_out));  // open: en
  Register #(.width(18)) register_2 (.D(Write_Data), .Q(register_2_q), .clk(Clock), .clr(and_2_out));  // open: en
  Register #(.width(18)) register_3 (.D(Write_Data), .Q(register_3_q), .clk(Clock), .clr(and_3_out));  // open: en
  Register #(.width(18)) register_4 (.D(Write_Data), .Q(register_4_q), .clk(Clock), .clr(and_4_out));  // open: en
  Register #(.width(18)) register_5 (.D(Write_Data), .Q(register_5_q), .clk(Clock), .clr(and_5_out));  // open: en
  Register #(.width(18)) register_6 (.D(Write_Data), .Q(register_6_q), .clk(Clock), .clr(and_6_out));  // open: en
  Register #(.width(18)) register_7 (.D(Write_Data), .Q(register_7_q), .clk(Clock), .clr(and_7_out));  // open: en
  and and_10 (and_10_out, decoder_1_out8, regWrite);
  and and_11 (and_11_out, decoder_1_out9, regWrite);
  and and_12 (and_12_out, decoder_1_out10, regWrite);
  Register #(.width(18)) register_8 (.D(Write_Data), .Q(register_8_q), .clk(Clock), .clr(and_8_out));  // open: en
  Register #(.width(18)) register_9 (.D(Write_Data), .Q(register_9_q), .clk(Clock), .clr(and_9_out));  // open: en
  and and_13 (and_13_out, decoder_1_out11, regWrite);
  and and_14 (and_14_out, decoder_1_out12, regWrite);
  and and_15 (and_15_out, decoder_1_out13, regWrite);
  and and_16 (and_16_out, decoder_1_out14, regWrite);
  and and_17 (and_17_out, decoder_1_out15, regWrite);
  and and_18 (and_18_out, decoder_1_out17, regWrite);
  Register #(.width(18)) register_10 (.D(Write_Data), .Q(register_10_q), .clk(Clock), .clr(and_10_out));  // open: en
  Register #(.width(18)) register_11 (.D(Write_Data), .Q(register_11_q), .clk(Clock), .clr(and_11_out));  // open: en
  Register #(.width(18)) register_12 (.D(Write_Data), .Q(register_12_q), .clk(Clock), .clr(and_12_out));  // open: en
  Register #(.width(18)) register_13 (.D(Write_Data), .Q(register_13_q), .clk(Clock), .clr(and_13_out));  // open: en
  Register #(.width(18)) register_14 (.D(Write_Data), .Q(register_14_q), .clk(Clock), .clr(and_14_out));  // open: en
  Register #(.width(18)) register_15 (.D(Write_Data), .Q(register_15_q), .clk(Clock), .clr(and_15_out));  // open: en
  Register #(.width(18)) register_16 (.D(Write_Data), .Q(register_16_q), .clk(Clock), .clr(and_16_out));  // open: en
  Register #(.width(18)) register_17 (.D(Write_Data), .Q(register_17_q), .clk(Clock), .clr(and_17_out));  // open: en
  Register #(.width(18)) register_18 (.D(Write_Data), .Q(register_18_q), .clk(Clock), .clr(and_18_out));  // open: en
  Multiplexer #(.select(5), .width(18)) multiplexer_1 (
    .in0(register_1_q), .in1(register_2_q), .in2(register_3_q), .in3(register_4_q), .in4(register_5_q),
    .in5(register_6_q), .in6(register_7_q), .in7(register_8_q), .in8(register_10_q), .in9(register_11_q),
    .in10(register_12_q), .in11(register_13_q), .in12(register_14_q), .in13(register_15_q),
    .in14(register_16_q), .in15(register_17_q), .in16(register_9_q), .in17(register_18_q), .out(read_data_1),
    .sel(read_register_1));  // open: in18, in19, in20, in21, in22, in23, in24, in25, in26, in27, in28, in29, in30, in31, en
  Multiplexer #(.select(5), .width(18)) multiplexer_2 (
    .in0(register_1_q), .in1(register_2_q), .in2(register_3_q), .in3(register_4_q), .in4(register_5_q),
    .in5(register_6_q), .in6(register_7_q), .in7(register_8_q), .in8(register_10_q), .in9(register_11_q),
    .in10(register_12_q), .in11(register_13_q), .in12(register_14_q), .in13(register_15_q),
    .in14(register_16_q), .in15(register_17_q), .in16(register_9_q), .in17(register_18_q), .out(read_data_2),
    .sel(read_register_2));  // open: in18, in19, in20, in21, in22, in23, in24, in25, in26, in27, in28, in29, in30, in31, en
endmodule

// ALU
module _1_bit_ALU (
  input  B,
  input  A,
  input  CarryIn,
  input  [1:0] Opcode,
  input  BInvert,
  output result,
  output carryOut
);

  wire adder_1_out, multiplexer_1_out, nor_1_out, not_1_out, or_1_out;

  not not_1 (not_1_out, B);
  Multiplexer multiplexer_1 (.in0(not_1_out), .in1(B), .out(multiplexer_1_out), .sel(BInvert));  // open: en
  or or_1 (or_1_out, A, B);
  nor nor_1 (nor_1_out, A, B);
  Adder #(.width(1)) adder_1 (.a(A), .b(multiplexer_1_out), .out(adder_1_out), .cin(CarryIn), .cout(carryOut));
  Multiplexer #(.select(2)) multiplexer_2 (
    .in0(or_1_out), .in1(nor_1_out), .in2(adder_1_out), .out(result), .sel(Opcode));  // open: in3, en
endmodule

module _18_bit_ALU (
  input  carryIn,
  input  [17:0] B,
  input  [17:0] A,
  input  Binvert,
  input  [1:0] Opcode,
  output [17:0] result,
  output zero,
  output overflow,
  output carryOut
);

  wire n1_bit_alu_1_carryout, n1_bit_alu_2_carryout, n1_bit_alu_3_carryout, n1_bit_alu_4_carryout,
       n1_bit_alu_5_carryout, n1_bit_alu_6_carryout, n1_bit_alu_7_carryout, n1_bit_alu_8_carryout,
       n1_bit_alu_9_carryout, n1_bit_alu_10_carryout, n1_bit_alu_11_carryout, n1_bit_alu_12_carryout,
       n1_bit_alu_13_carryout, n1_bit_alu_14_carryout, n1_bit_alu_15_carryout, n1_bit_alu_16_carryout,
       n1_bit_alu_17_carryout;

  _1_bit_ALU u_1_bit_alu_1 (
    .result(result[0]), .B(B[0]), .A(A[0]), .CarryIn(carryIn), .BInvert(Binvert),
    .carryOut(n1_bit_alu_1_carryout), .Opcode(Opcode));
  _1_bit_ALU u_1_bit_alu_2 (
    .result(result[1]), .B(B[1]), .A(A[1]), .CarryIn(n1_bit_alu_1_carryout), .BInvert(Binvert),
    .carryOut(n1_bit_alu_2_carryout), .Opcode(Opcode));
  _1_bit_ALU u_1_bit_alu_3 (
    .result(result[2]), .B(B[2]), .A(A[2]), .CarryIn(n1_bit_alu_2_carryout), .BInvert(Binvert),
    .carryOut(n1_bit_alu_3_carryout), .Opcode(Opcode));
  _1_bit_ALU u_1_bit_alu_4 (
    .result(result[3]), .B(B[3]), .A(A[3]), .CarryIn(n1_bit_alu_3_carryout), .BInvert(Binvert),
    .carryOut(n1_bit_alu_4_carryout), .Opcode(Opcode));
  _1_bit_ALU u_1_bit_alu_5 (
    .result(result[4]), .B(B[4]), .A(A[4]), .CarryIn(n1_bit_alu_4_carryout), .BInvert(Binvert),
    .carryOut(n1_bit_alu_5_carryout), .Opcode(Opcode));
  _1_bit_ALU u_1_bit_alu_6 (
    .result(result[5]), .B(B[5]), .A(A[5]), .CarryIn(n1_bit_alu_5_carryout), .BInvert(Binvert),
    .carryOut(n1_bit_alu_6_carryout), .Opcode(Opcode));
  _1_bit_ALU u_1_bit_alu_7 (
    .result(result[6]), .B(B[6]), .A(A[6]), .CarryIn(n1_bit_alu_6_carryout), .BInvert(Binvert),
    .carryOut(n1_bit_alu_7_carryout), .Opcode(Opcode));
  _1_bit_ALU u_1_bit_alu_8 (
    .result(result[7]), .B(B[7]), .A(A[7]), .CarryIn(n1_bit_alu_7_carryout), .BInvert(Binvert),
    .carryOut(n1_bit_alu_8_carryout), .Opcode(Opcode));
  _1_bit_ALU u_1_bit_alu_9 (
    .result(result[8]), .B(B[8]), .A(A[8]), .CarryIn(n1_bit_alu_8_carryout), .BInvert(Binvert),
    .carryOut(n1_bit_alu_9_carryout), .Opcode(Opcode));
  _1_bit_ALU u_1_bit_alu_10 (
    .result(result[9]), .B(B[9]), .A(A[9]), .CarryIn(n1_bit_alu_9_carryout), .BInvert(Binvert),
    .carryOut(n1_bit_alu_10_carryout), .Opcode(Opcode));
  _1_bit_ALU u_1_bit_alu_11 (
    .result(result[10]), .B(B[10]), .A(A[10]), .CarryIn(n1_bit_alu_10_carryout), .BInvert(Binvert),
    .carryOut(n1_bit_alu_11_carryout), .Opcode(Opcode));
  _1_bit_ALU u_1_bit_alu_12 (
    .result(result[11]), .B(B[11]), .A(A[11]), .CarryIn(n1_bit_alu_11_carryout), .BInvert(Binvert),
    .carryOut(n1_bit_alu_12_carryout), .Opcode(Opcode));
  _1_bit_ALU u_1_bit_alu_13 (
    .result(result[12]), .B(B[12]), .A(A[12]), .CarryIn(n1_bit_alu_12_carryout), .BInvert(Binvert),
    .carryOut(n1_bit_alu_13_carryout), .Opcode(Opcode));
  _1_bit_ALU u_1_bit_alu_14 (
    .result(result[13]), .B(B[13]), .A(A[13]), .CarryIn(n1_bit_alu_13_carryout), .BInvert(Binvert),
    .carryOut(n1_bit_alu_14_carryout), .Opcode(Opcode));
  _1_bit_ALU u_1_bit_alu_15 (
    .result(result[14]), .B(B[14]), .A(A[14]), .CarryIn(n1_bit_alu_14_carryout), .BInvert(Binvert),
    .carryOut(n1_bit_alu_15_carryout), .Opcode(Opcode));
  _1_bit_ALU u_1_bit_alu_16 (
    .result(result[15]), .B(B[15]), .A(A[15]), .CarryIn(n1_bit_alu_15_carryout), .BInvert(Binvert),
    .carryOut(n1_bit_alu_16_carryout), .Opcode(Opcode));
  _1_bit_ALU u_1_bit_alu_17 (
    .result(result[16]), .B(B[16]), .A(A[16]), .CarryIn(n1_bit_alu_16_carryout), .BInvert(Binvert),
    .carryOut(n1_bit_alu_17_carryout), .Opcode(Opcode));
  _1_bit_ALU u_1_bit_alu_18 (
    .result(result[17]), .B(B[17]), .A(A[17]), .CarryIn(n1_bit_alu_17_carryout), .BInvert(Binvert),
    .carryOut(carryOut), .Opcode(Opcode));
  xor xor_1 (overflow, n1_bit_alu_17_carryout, carryOut);
  nor nor_1 (zero, result[0], result[1], result[2], result[3], result[4], result[5], result[6], result[7], result[8], result[9], result[10], result[11], result[12], result[13], result[14], result[15], result[16], result[17]);
endmodule

module Alu_imp (
  input  carryin,
  input  [17:0] Operand_A,
  input  [17:0] Operand_B,
  input  Binvert,
  input  [1:0] Opcode,
  output [17:0] result,
  output zero,
  output overflow,
  output carryOut
);

  _18_bit_ALU u_18_bit_alu_1 (
    .B(Operand_A), .A(Operand_B), .Binvert(Binvert), .Opcode(Opcode), .result(result), .zero(zero),
    .overflow(overflow), .carryOut(carryOut), .carryIn(carryin));
endmodule
