// Logisim project 2 bit logic unit.circ as structural Verilog: 2 circuits, main circuit main
module main (
  input  B1,
  input  A1,
  input  B0,
  input  A0,
  input  [1:0] Select_Bits,
  output F1,
  output [1:0] out_7,
  output F2
);

  wire and_1_out, and_2_out, not_1_out, not_2_out, or_1_out, or_2_out, xor_1_out, xor_2_out;

  and and_1 (and_1_out, B1, A1);
  or or_1 (or_1_out, B1, A1);
  xor xor_1 (xor_1_out, B1, A1);
  not not_1 (not_1_out, B1);
  and and_2 (and_2_out, B0, A0);
  or or_2 (or_2_out, B0, A0);
  xor xor_2 (xor_2_out, B0, A0);
  not not_2 (not_2_out, B0);
  Multiplexer #(.select(2)) multiplexer_1 (
    .in0(and_2_out), .in1(or_2_out), .in2(xor_2_out), .in3(not_2_out), .out(F2), .sel(Select_Bits));  // open: en
  Multiplexer #(.select(2)) multiplexer_2 (
    .in0(and_1_out), .in1(or_1_out), .in2(xor_1_out), .in3(not_1_out), .out(F1), .sel(Select_Bits));  // open: en

  assign out_7 = {F2, F1};
endmodule

module Imp (
  input  in_1,
  input  in_2,
  input  in_3,
  input  in_4,
  input  [1:0] in_5,
  output out_6,
  output [1:0] out_7,
  output out_8
);

  main main_1 (.B1(in_1), .A1(in_2), .B0(in_3), .A0(in_4), .Select_Bits(in_5), .F1(out_6), .out_7(out_7), .F2(out_8));
endmodule
