// Logisim project 4bitArithmaticUnit.circ as structural Verilog: 2 circuits, main circuit main
module main (
  input  Cin,
  input  [1:0] Selection_Bits,
  input  A0,
  input  B0,
  input  A1,
  input  B1,
  input  A2,
  input  b2,
  input  A3,
  input  B3,
  input  F1,
  output [3:0] Result,
  output Cout
);

  wire adder_1_cout, adder_2_cout, adder_3_cout, multiplexer_1_out, multiplexer_2_out, multiplexer_3_out,
       multiplexer_4_out, not_1_out, not_2_out, not_3_out, not_4_out, not_5_out;

  not not_1 (not_1_out, B1);
  not not_2 (not_2_out, B0);
  not not_3 (not_3_out, b2);
  not not_4 (not_4_out, B3);
  not not_5 (not_5_out, F1);
  Multiplexer #(.select(2), .enable("false")) multiplexer_1 (
    .in0(B0), .in1(not_2_out), .in3(F1), .out(multiplexer_1_out), .sel(Selection_Bits));  // open: in2
  Multiplexer #(.select(2), .enable("false")) multiplexer_2 (
    .in0(B1), .in1(not_1_out), .in3(F1), .out(multiplexer_2_out), .sel(Selection_Bits));  // open: in2
  Multiplexer #(.select(2), .enable("false")) multiplexer_3 (
    .in0(b2), .in1(not_3_out), .in2(F1), .out(multiplexer_3_out), .sel(Selection_Bits));  // open: in3
  Multiplexer #(.select(2), .enable("false")) multiplexer_4 (
    .in0(B3), .in1(not_4_out), .in2(F1), .in3(not_5_out), .out(multiplexer_4_out), .sel(Selection_Bits));
  Adder #(.width(1)) adder_1 (.a(A0), .b(multiplexer_1_out), .out(Result[0]), .cin(Cin), .cout(adder_1_cout));
  Adder #(.width(1)) adder_2 (.a(A1), .b(multiplexer_2_out), .out(Result[1]), .cin(adder_1_cout), .cout(adder_2_cout));
  Adder #(.width(1)) adder_3 (.a(A2), .b(multiplexer_3_out), .out(Result[2]), .cin(adder_2_cout), .cout(adder_3_cout));
  Adder #(.width(1)) adder_4 (.a(A3), .b(multiplexer_4_out), .out(Result[3]), .cin(adder_3_cout), .cout(Cout));
endmodule

module Imp (
  input  in_1,
  input  [1:0] in_2,
  input  in_3,
  input  in_4,
  input  in_5,
  input  in_6,
  input  in_7,
  input  in_8,
  input  in_9,
  input  in_10,
  input  in_11,
  output [3:0] out_12,
  output out_13
);

  main main_1 (
    .Cin(in_1), .Selection_Bits(in_2), .A0(in_3), .B0(in_4), .A1(in_6), .B1(in_9), .A2(in_11), .b2(in_8),
    .A3(in_10), .B3(in_7), .F1(in_5), .Result(out_12), .Cout(out_13));
endmodule
