// Logisim project 4 bit multiplier.circ as structural Verilog: 2 circuits, main circuit main
module main (
  input  B0,
  input  B1,
  input  B2,
  input  B3,
  input  A3,
  input  A2,
  input  A1,
  input  A0,
  output S0,
  output S3,
  output S2,
  output S1,
  output S5,
  output S4,
  output S6,
  output S7
);

  wire adder_1_cout, adder_1_out, adder_2_cout, adder_2_out, adder_3_cout, adder_4_cout, adder_5_cout,
       adder_5_out, adder_6_cout, adder_7_cout, adder_8_cout, and_1_out, and_2_out, and_3_out, and_4_out,
       and_5_out, and_6_out, and_7_out, and_8_out, and_9_out, and_10_out, and_12_out, and_13_out, and_15_out,
       and_17_out;

  and and_1 (and_1_out, A3, B2);
  Adder #(.width(1)) adder_1 (.a(and_5_out), .b(and_7_out), .out(adder_1_out), .cin(adder_6_cout), .cout(adder_1_cout));
  and and_2 (and_2_out, A1, B3);
  and and_3 (and_3_out, A2, B3);
  and and_4 (and_4_out, A0, B2);
  and and_5 (and_5_out, A3, B0);
  and and_6 (and_6_out, A3, B3);
  and and_7 (and_7_out, A2, B1);
  and and_8 (and_8_out, A3, B1);
  and and_9 (and_9_out, A2, B0);
  and and_10 (and_10_out, A1, B2);
  // AND_Gate and_11 has open pins: in0=A0, in1=B3, out=open
  and and_12 (and_12_out, A2, B2);
  and and_13 (and_13_out, A1, B1);
  Adder #(.width(1)) adder_2 (
    .a(and_12_out), .b(and_8_out), .out(adder_2_out), .cin(adder_3_cout), .cout(adder_2_cout));
  and and_14 (S7, and_6_out, adder_4_cout);
  Adder #(.width(1)) adder_3 (.a(adder_1_out), .b(and_10_out), .out(S3), .cin(adder_1_cout), .cout(adder_3_cout));
  Adder #(.width(1)) adder_4 (.a(and_3_out), .b(and_1_out), .out(S5), .cin(adder_7_cout), .cout(adder_4_cout));
  xor xor_1 (S6, adder_4_cout, and_6_out);
  Adder #(.width(1)) adder_5 (
    .a(and_13_out), .b(and_9_out), .out(adder_5_out), .cin(adder_8_cout), .cout(adder_5_cout));
  Adder #(.width(1)) adder_6 (.a(adder_5_out), .b(and_4_out), .out(S2), .cin(adder_5_cout), .cout(adder_6_cout));
  Adder #(.width(1)) adder_7 (.a(adder_2_out), .b(and_2_out), .out(S4), .cin(adder_2_cout), .cout(adder_7_cout));
  and and_15 (and_15_out, A0, B1);
  and and_16 (S0, A0, B0);
  and and_17 (and_17_out, A1, B0);
  Adder #(.width(1)) adder_8 (.a(and_17_out), .b(and_15_out), .out(S1), .cout(adder_8_cout));  // open: cin
endmodule

module Imp (
  input  B0,
  input  B1,
  input  B2,
  input  B3,
  input  A0,
  input  A1,
  input  A2,
  input  A3,
  output S0,
  output S3,
  output S1,
  output S4,
  output S2,
  output S5,
  output S6,
  output S7
);

  main main_1 (
    .A3(A3), .A2(A2), .A1(A0), .A0(A0), .B0(B0), .B1(B1), .B2(B2), .B3(B3), .S0(S0), .S3(S1), .S2(S2),
    .S1(S3), .S5(S4), .S4(S5), .S6(S6), .S7(S7));

  assign A1 = A0;
endmodule
