// Logisim project 2 bit Register File Design.circ as structural Verilog: 1 circuit, main circuit main
module main (
  input  [1:0] write_data,
  input  [1:0] read_register_1,
  input  Enabler,
  input  [1:0] write_register,
  input  [1:0] read_register_2,
  output [1:0] read_data_1,
  output [1:0] read_data_2
);

  wire Clock_out, demultiplexer_1_out0, demultiplexer_1_out1, demultiplexer_1_out2, demultiplexer_1_out3;
  wire [1:0] register_1_q, register_2_q, register_3_q, register_4_q;

  Demultiplexer #(.select(2), .enable("false")) demultiplexer_1 (
    .out0(demultiplexer_1_out0), .out1(demultiplexer_1_out1), .out2(demultiplexer_1_out2),
    .out3(demultiplexer_1_out3), .in(Enabler), .sel(write_register));
  Clock Clock (.out(Clock_out));
  Register #(.width(2)) register_1 (
    .D(write_data), .en(demultiplexer_1_out0), .Q(register_1_q), .clk(Clock_out));  // open: clr
  Register #(.width(2)) register_2 (
    .D(write_data), .en(demultiplexer_1_out1), .Q(register_2_q), .clk(Clock_out));  // open: clr
  Register #(.width(2)) register_3 (
    .D(write_data), .en(demultiplexer_1_out2), .Q(register_3_q), .clk(Clock_out));  // open: clr
  Register #(.width(2)) register_4 (
    .D(write_data), .en(demultiplexer_1_out3), .Q(register_4_q), .clk(Clock_out));  // open: clr
  Multiplexer #(.select(2), .width(2), .enable("false")) multiplexer_1 (
    .in0(register_1_q), .in1(register_2_q), .in2(register_3_q), .in3(register_4_q), .out(read_data_1),
    .sel(read_register_1));
  Multiplexer #(.select(2), .width(2), .enable("false")) multiplexer_2 (
    .in0(register_1_q), .in1(register_2_q), .in2(register_3_q), .in3(register_4_q), .out(read_data_2),
    .sel(read_register_2));
endmodule
